# Fritzing sketch circuit (saved by Fritzing 0.9.4)
breadboards: 1

parts:
  Part1 = Photon
  Part2 = ws2812b [package="smd 2812b"]

nets:
  GND: Part1.GND, Part2.VSS
  N1: Part1.D6, Part2.DIN
  3V3: Part1.3V3, Part2.VDD
